// Logisim project uart_glue_logic.circ as structural Verilog: 1 circuit, main circuit main
module main (
  input  [15:0] ADDR_BUS,
  input  n_WRAM,
  input  CPU_RST,
  input  INTR,
  input  DR,
  input  [7:0] DATA_BUS,
  output n_CSO,
  output [1:0] ADDR,
  output n_RD,
  output n_WR,
  output RST,
  output n_IRQ4,
  output n_IRQ5,
  output [7:0] DATA
);

  wire n_CLK_out, nand_1_out, nor_1_out, not_2_out, not_3_out;

  Clock n_CLK (.out(n_CLK_out));
  // NoConnect on ADDR_BUS[7:2]
  nor nor_1 (nor_1_out, ~ADDR_BUS[15], ~ADDR_BUS[14], ADDR_BUS[13], ADDR_BUS[12], ADDR_BUS[11], ADDR_BUS[10], ADDR_BUS[9], ~ADDR_BUS[8]);  // NOR_Gate
  // Probe on nor_1_out
  not not_1 (n_CSO, nor_1_out);
  nand nand_1 (nand_1_out, nor_1_out, n_CLK_out);
  not not_2 (not_2_out, nand_1_out);
  nand nand_2 (n_RD, not_2_out, n_WRAM);
  nand nand_3 (n_WR, not_2_out, not_3_out);
  not not_3 (not_3_out, n_WRAM);
  not not_4 (n_IRQ4, INTR);
  not not_5 (n_IRQ5, DR);

  assign ADDR = ADDR_BUS[1:0];
  assign DATA = DATA_BUS;
  assign RST = CPU_RST;

  // Notes on the sheet:
  //   n_WRAM: initial=0x1
  //   CPU_RST: initial=0x1
  //   DATA_BUS: initial=0xff
  //   ADDR_BUS: initial=0xffff
endmodule
